# Fritzing sketch IDD (saved by Fritzing 0.9.4)
breadboards: 1

parts:
  WeMos_D1_Mini1 = WeMos D1 Mini
  S1 = Square Pushbutton
  R1 = Resistor [tolerance=±5% resistance=330 package="0603 [SMD]"]
  R2 = Resistor [tolerance=±5% resistance=1k package="0603 [SMD]"]
  LED1 = smd LED [color="Red (633nm)" package="1206 [SMD]"]

nets:
  N1: WeMos_D1_Mini1.D5, S1.leg0, R1.Pin_0
  N2: R1.Pin_1, R2.Pin_0
  N3: R2.Pin_1, LED1.cathode
